# Fritzing sketch schematic (saved by Fritzing 0.9.3b)
breadboards: 1

parts:
  Line-in_input_(stereo) = 2.5mm Audio Jack [package=stereojack2.5mm_specia_pogopins]
  Line-in_volume = POT [package=pot_alpha_rv16af-20]
  R1 = Resistor [tolerance=±5% resistance=100 package="2512 [SMD]"]
  Source_input_(stereo) = 2.5mm Audio Jack [package=stereojack2.5mm_specia_pogopins]
  Source_volume = POT [package=pot_alpha_rv16af-20]
  R2 = Resistor [tolerance=±5% resistance=100 package="2512 [SMD]"]
  Mix_volume = POT [package=pot_alpha_rv16af-20]
  Mix_output_(mono) = 2.5mm Audio Jack [package=stereojack2.5mm_specia_pogopins]
  Sync_output_(stereo) = 2.5mm Audio Jack [package=stereojack2.5mm_specia_pogopins]
  Arduino = Arduino Uno (Rev3)
  VCC1 = Battery block 9V
  D1 = Diode [package=diode-1n4001]
  Rotary_Encoder_(PEL12D-4225S-S2024) = ENCODER_2LED [package=encoder_led_2]
  Bauteil1 = 0.56" 7-segment LED Backpack [part_number=1002]

nets:
  GND: Line-in_input_(stereo).SLEEVE, Line-in_input_(stereo).RIGHT, Line-in_volume.A, Source_input_(stereo).SLEEVE, Source_input_(stereo).RIGHT, Source_volume.A, Mix_volume.A, Mix_output_(mono).SLEEVE, Mix_output_(mono).RIGHT, Sync_output_(stereo).SLEEVE, Arduino.GND, VCC1.-, Rotary_Encoder_(PEL12D-4225S-S2024).C, Rotary_Encoder_(PEL12D-4225S-S2024).-, Bauteil1.GND
  N1: Line-in_input_(stereo).LEFT, Line-in_volume.E
  N2: Line-in_volume.S, R1.Pin_0
  N3: R1.Pin_1, R2.Pin_1, Mix_volume.E
  N4: Source_input_(stereo).LEFT, Source_volume.E
  N5: Source_volume.S, R2.Pin_0
  N6: Mix_volume.S, Mix_output_(mono).LEFT
  N7: Sync_output_(stereo).LEFT, Arduino.D13/SCK
  Channel left: Arduino.A0
  Channel right: Arduino.A1
  N8: Arduino.A4/SDA, Bauteil1.SDA
  N9: Arduino.A5/SCL, Bauteil1.SCL
  N10: Arduino.D8, Rotary_Encoder_(PEL12D-4225S-S2024).+G
  N11: Arduino.D12/MISO, Rotary_Encoder_(PEL12D-4225S-S2024).SW
  N12: Arduino.D2, Rotary_Encoder_(PEL12D-4225S-S2024).A
  N13: Arduino.D3_PWM, Rotary_Encoder_(PEL12D-4225S-S2024).B
  Strobe: Arduino.D4
  Reset: Arduino.D5_PWM
  5V: Arduino.5V, Bauteil1.VDD
  N14: Arduino.VIN, D1.A
  N15: VCC1.+, D1.C

custom parts:
  0.56" 7-segment LED Backpack: This 0.56" 7-segment LED display includes a driver chip for simple control via an I2C interface. The backpack features address-selection jumpers so you can connect up to eight displays on a single I2C bus.
